// Logisim project batalha_naval_final.circ as structural Verilog: 1 circuit, main circuit main
module main (
  input  A,
  input  in_2,
  input  in_3,
  input  B,
  input  C,
  input  in_6,
  input  D,
  input  in_8,
  input  in_9,
  input  in_10,
  input  in_11,
  input  in_12,
  input  Disparo
);

  wire and_1_out, and_2_out, and_3_out, and_4_out, and_5_out, and_6_out, and_7_out, and_8_out, and_9_out,
       and_10_out, and_11_out, and_12_out, and_13_out, and_14_out, and_15_out, and_16_out, and_17_out,
       and_18_out, and_19_out, and_20_out, and_21_out, and_22_out, and_23_out, and_24_out, and_25_out,
       and_26_out, and_27_out, and_28_out, and_29_out, and_30_out, and_31_out, and_32_out, and_33_out,
       and_34_out, and_35_out, and_36_out, and_37_out, and_38_out, and_39_out, and_40_out, and_41_out,
       and_42_out, and_43_out, and_44_out, and_45_out, and_46_out, and_47_out, and_48_out, not_1_out,
       not_2_out, not_3_out, not_4_out, not_5_out, not_6_out, not_7_out, not_8_out, not_9_out, not_10_out,
       not_11_out, not_12_out, not_13_out, not_14_out, not_15_out, not_16_out, not_17_out, not_18_out,
       not_19_out, not_20_out, not_21_out, not_22_out, not_23_out, not_24_out, not_25_out, not_26_out,
       not_27_out, not_28_out, not_29_out, not_30_out, not_31_out, not_32_out, not_33_out, not_34_out,
       not_35_out, not_36_out, not_37_out, not_38_out, not_39_out, not_40_out, not_41_out, not_42_out,
       not_43_out, not_44_out, not_45_out, not_46_out, not_47_out, not_48_out, not_49_out, not_50_out,
       not_51_out, not_52_out, not_53_out, not_54_out, not_55_out, not_56_out, not_57_out, not_58_out,
       not_59_out, not_60_out, not_61_out, or_1_out, or_2_out, or_3_out, or_4_out, or_5_out, or_6_out,
       or_7_out, or_8_out, or_9_out, xnor_1_out, xnor_2_out, xnor_3_out, xnor_4_out, xnor_5_out, xnor_6_out,
       xnor_7_out, xnor_8_out;

  not not_1 (not_1_out, A);
  not not_2 (not_2_out, in_3);
  not not_3 (not_3_out, A);
  not not_4 (not_4_out, in_3);
  not not_5 (not_5_out, A);
  not not_6 (not_6_out, C);
  not not_7 (not_7_out, D);
  not not_8 (not_8_out, in_3);
  not not_9 (not_9_out, C);
  not not_10 (not_10_out, D);
  not not_11 (not_11_out, C);
  not not_12 (not_12_out, D);
  not not_13 (not_13_out, in_3);
  not not_14 (not_14_out, C);
  and and_1 (and_1_out, not_13_out, not_14_out, not_15_out);
  not not_15 (not_15_out, D);
  not not_16 (not_16_out, A);
  not not_17 (not_17_out, in_3);
  and and_2 (and_2_out, not_16_out, not_17_out, C);
  not not_18 (not_18_out, A);
  and and_3 (and_3_out, not_18_out, C, not_19_out);
  not not_19 (not_19_out, D);
  not not_20 (not_20_out, C);
  and and_4 (and_4_out, in_3, not_20_out, D);
  not not_21 (not_21_out, in_3);
  and and_5 (and_5_out, A, not_21_out, not_22_out);
  not not_22 (not_22_out, C);
  not not_23 (not_23_out, in_3);
  and and_6 (and_6_out, not_23_out, C);
  not not_24 (not_24_out, A);
  and and_7 (and_7_out, not_24_out, in_3, not_25_out);
  not not_25 (not_25_out, C);
  not not_26 (not_26_out, in_3);
  and and_8 (and_8_out, A, not_26_out, D);
  and and_9 (and_9_out, A, C, D);
  not not_27 (not_27_out, A);
  not not_28 (not_28_out, in_3);
  and and_10 (and_10_out, not_27_out, not_28_out, not_29_out);
  not not_29 (not_29_out, D);
  not not_30 (not_30_out, C);
  and and_11 (and_11_out, in_3, not_30_out, D);
  and and_12 (and_12_out, A, C, D);
  and and_13 (and_13_out, A, in_3);
  and and_14 (and_14_out, not_1_out, not_2_out, C);
  and and_15 (and_15_out, not_3_out, C, D);
  and and_16 (and_16_out, not_4_out, C, D);
  and and_17 (and_17_out, not_5_out, in_3, not_6_out, not_7_out);
  and and_18 (and_18_out, A, not_8_out, not_9_out, not_10_out);
  and and_19 (and_19_out, A, in_3, not_11_out, D);
  and and_20 (and_20_out, A, in_3, C, not_12_out);
  or or_1 (or_1_out, and_1_out, and_2_out, and_3_out, and_4_out, and_5_out);
  or or_2 (or_2_out, and_6_out, and_7_out, and_8_out, and_9_out);
  or or_3 (or_3_out, and_10_out, and_11_out, and_12_out, and_13_out);
  or or_4 (or_4_out, and_14_out, and_15_out, and_16_out, and_17_out, and_18_out, and_19_out, and_20_out);
  xnor xnor_1 (xnor_1_out, or_4_out, and_22_out);
  xnor xnor_2 (xnor_2_out, or_1_out, and_23_out);
  and and_21 (and_21_out, xnor_1_out, xnor_2_out, xnor_3_out, xnor_4_out);
  xnor xnor_3 (xnor_3_out, or_2_out, and_44_out);
  xnor xnor_4 (xnor_4_out, or_3_out, and_45_out);
  and and_22 (and_22_out, Disparo, in_9);
  not not_31 (not_31_out, in_2);
  not not_32 (not_32_out, B);
  not not_33 (not_33_out, in_2);
  not not_34 (not_34_out, B);
  not not_35 (not_35_out, in_2);
  not not_36 (not_36_out, in_6);
  not not_37 (not_37_out, in_8);
  not not_38 (not_38_out, B);
  not not_39 (not_39_out, in_6);
  not not_40 (not_40_out, in_8);
  not not_41 (not_41_out, in_6);
  not not_42 (not_42_out, in_8);
  not not_43 (not_43_out, B);
  not not_44 (not_44_out, in_6);
  not not_45 (not_45_out, in_8);
  not not_46 (not_46_out, in_2);
  not not_47 (not_47_out, B);
  not not_48 (not_48_out, in_2);
  not not_49 (not_49_out, in_8);
  not not_50 (not_50_out, in_6);
  not not_51 (not_51_out, B);
  not not_52 (not_52_out, in_6);
  not not_53 (not_53_out, B);
  not not_54 (not_54_out, in_2);
  not not_55 (not_55_out, in_6);
  not not_56 (not_56_out, B);
  not not_57 (not_57_out, in_2);
  not not_58 (not_58_out, B);
  not not_59 (not_59_out, in_8);
  not not_60 (not_60_out, in_6);
  and and_23 (and_23_out, Disparo, in_10);
  and and_24 (and_24_out, not_31_out, not_32_out, in_6);
  and and_25 (and_25_out, not_33_out, in_6, in_8);
  and and_26 (and_26_out, not_34_out, in_6, in_8);
  and and_27 (and_27_out, not_35_out, B, not_36_out, not_37_out);
  and and_28 (and_28_out, in_2, not_38_out, not_39_out, not_40_out);
  and and_29 (and_29_out, in_2, B, not_41_out, in_8);
  and and_30 (and_30_out, in_2, B, in_6, not_42_out);
  and and_31 (and_31_out, not_43_out, not_44_out, not_45_out);
  and and_32 (and_32_out, not_46_out, not_47_out, in_6);
  and and_33 (and_33_out, not_48_out, in_6, not_49_out);
  and and_34 (and_34_out, B, not_50_out, in_8);
  and and_35 (and_35_out, in_2, not_51_out, not_52_out);
  and and_36 (and_36_out, not_53_out, in_6);
  and and_37 (and_37_out, not_54_out, B, not_55_out);
  and and_38 (and_38_out, in_2, not_56_out, in_8);
  and and_39 (and_39_out, in_2, in_6, in_8);
  and and_40 (and_40_out, not_57_out, not_58_out, not_59_out);
  and and_41 (and_41_out, B, not_60_out, in_8);
  and and_42 (and_42_out, in_2, in_6, in_8);
  and and_43 (and_43_out, in_2, B);
  and and_44 (and_44_out, Disparo, in_11);
  or or_5 (or_5_out, and_21_out, and_48_out);
  not not_61 (not_61_out, or_5_out);
  or or_6 (or_6_out, and_24_out, and_25_out, and_26_out, and_27_out, and_28_out, and_29_out, and_30_out);
  or or_7 (or_7_out, and_31_out, and_32_out, and_33_out, and_34_out, and_35_out);
  or or_8 (or_8_out, and_36_out, and_37_out, and_38_out, and_39_out);
  or or_9 (or_9_out, and_40_out, and_41_out, and_42_out, and_43_out);
  and and_45 (and_45_out, Disparo, in_12);
  and and_46 (and_46_out, not_61_out, Disparo);
  and and_47 (and_47_out, or_5_out, Disparo);
  xnor xnor_5 (xnor_5_out, or_6_out, and_22_out);
  LED Errou (.in(and_46_out));
  LED Acertou (.in(and_47_out));
  xnor xnor_6 (xnor_6_out, or_7_out, and_23_out);
  and and_48 (and_48_out, xnor_5_out, xnor_6_out, xnor_7_out, xnor_8_out);
  xnor xnor_7 (xnor_7_out, or_8_out, and_44_out);
  xnor xnor_8 (xnor_8_out, or_9_out, and_45_out);
endmodule
