// Logisim project CircuitoRegroupement.circ as structural Verilog: 1 circuit, main circuit main
module main (
  input  A,
  input  E,
  input  B,
  input  F,
  input  C,
  input  G,
  input  D,
  input  H,
  input  in_9,
  input  in_10,
  input  in_11,
  input  in_12,
  input  Disparo
);

  wire and_1_out, and_2_out, and_3_out, and_4_out, and_5_out, and_6_out, and_7_out, not_1_out, or_1_out,
       xnor_1_out, xnor_2_out, xnor_3_out, xnor_4_out, xnor_5_out, xnor_6_out, xnor_7_out, xnor_8_out;

  xnor xnor_1 (xnor_1_out, A, and_2_out);
  xnor xnor_2 (xnor_2_out, B, and_3_out);
  and and_1 (and_1_out, xnor_1_out, xnor_2_out, xnor_3_out, xnor_4_out);
  xnor xnor_3 (xnor_3_out, C, and_4_out);
  xnor xnor_4 (xnor_4_out, D, and_5_out);
  and and_2 (and_2_out, Disparo, in_9);
  and and_3 (and_3_out, Disparo, in_10);
  and and_4 (and_4_out, Disparo, in_11);
  or or_1 (or_1_out, and_1_out, and_7_out);
  not not_1 (not_1_out, or_1_out);
  and and_5 (and_5_out, Disparo, in_12);
  and and_6 (and_6_out, not_1_out, Disparo);
  xnor xnor_5 (xnor_5_out, E, and_2_out);
  LED Errou (.in(and_6_out));
  xnor xnor_6 (xnor_6_out, F, and_3_out);
  and and_7 (and_7_out, xnor_5_out, xnor_6_out, xnor_7_out, xnor_8_out);
  LED Acertou (.in(or_1_out));
  xnor xnor_7 (xnor_7_out, G, and_4_out);
  xnor xnor_8 (xnor_8_out, H, and_5_out);
endmodule
